// Logisim project ALU_01.circ as structural Verilog: 2 circuits, main circuit main
module main (
  input  load,
  input  in_2,
  input  [7:0] AND,
  input  [7:0] SUM,
  input  NO,
  input  f,
  output [7:0] OUT,
  output [7:0] OUT_2
);

  wire [7:0] not_1_out, not_2_out;

  Clock clock_1 ();  // open: out
  assign not_1_out = ~AND;  // NOT_Gate not_1, 8 bits wide
  assign not_2_out = ~SUM;  // NOT_Gate not_2, 8 bits wide
  Multiplexer #(.select(2), .width(8), .enable("false")) multiplexer_1 (
    .in0(AND), .in1(not_1_out), .in2(SUM), .in3(not_2_out), .out(OUT_2), .sel({f, NO}));
endmodule

module Not8 (
);

  wire not_1_out, not_2_out, not_3_out, not_4_out, not_5_out, not_6_out, not_7_out, not_8_out, undriven,
       undriven_2, undriven_3, undriven_4, undriven_5, undriven_6, undriven_7, undriven_8;

  not not_1 (not_1_out, undriven);
  not not_2 (not_2_out, undriven_2);
  not not_3 (not_3_out, undriven_3);
  not not_4 (not_4_out, undriven_4);
  not not_5 (not_5_out, undriven_5);
  not not_6 (not_6_out, undriven_6);
  not not_7 (not_7_out, undriven_7);
  not not_8 (not_8_out, undriven_8);
endmodule
