// Logisim project Adder-8-bits.circ as structural Verilog: 1 circuit, main circuit main
module main (
  input  [7:0] A,
  input  [7:0] B,
  output [7:0] out_3,
  output OVERFLOW
);

  wire adder_1_cout, adder_2_cout, adder_3_cout, adder_4_cout, adder_5_cout, adder_6_cout, and_1_out;

  xor xor_1 (out_3[0], A[0], B[0]);
  and and_1 (and_1_out, A[0], B[0]);
  Adder #(.width(1)) adder_1 (.a(A[1]), .b(B[1]), .out(out_3[1]), .cin(and_1_out), .cout(adder_1_cout));
  Adder #(.width(1)) adder_2 (.a(A[2]), .b(B[2]), .out(out_3[2]), .cin(adder_1_cout), .cout(adder_2_cout));
  Adder #(.width(1)) adder_3 (.a(A[3]), .b(B[3]), .out(out_3[3]), .cin(adder_2_cout), .cout(adder_3_cout));
  Adder #(.width(1)) adder_4 (.a(A[4]), .b(B[4]), .out(out_3[4]), .cin(adder_3_cout), .cout(adder_4_cout));
  Adder #(.width(1)) adder_5 (.a(A[5]), .b(B[5]), .out(out_3[5]), .cin(adder_4_cout), .cout(adder_5_cout));
  Adder #(.width(1)) adder_6 (.a(A[6]), .b(B[6]), .out(out_3[6]), .cin(adder_5_cout), .cout(adder_6_cout));
  Adder #(.width(1)) adder_7 (.a(A[7]), .b(B[7]), .out(out_3[7]), .cin(adder_6_cout), .cout(OVERFLOW));
endmodule
