// Logisim project Adder_Plus_One.circ as structural Verilog: 1 circuit, main circuit main
module main (
  input  [7:0] A,
  input  [7:0] B,
  output [7:0] out_3,
  output OVERFLOW,
  output OVERFLOW_2
);

  wire adder_1_cout, adder_2_cout, adder_3_cout, adder_4_cout, adder_5_cout, adder_6_cout, and_1_out;
  wire [7:0] not_1_out, xor_1_out;

  assign not_1_out = ~A;  // NOT_Gate not_1, 8 bits wide
  Button button_1 (.out(OVERFLOW_2));
  xor xor_1 (xor_1_out[0], not_1_out[0], B[0]);
  and and_1 (and_1_out, not_1_out[0], B[0]);
  Adder #(.width(1)) adder_1 (.a(not_1_out[1]), .b(B[1]), .out(xor_1_out[1]), .cin(and_1_out), .cout(adder_1_cout));
  Adder #(.width(1)) adder_2 (.a(not_1_out[2]), .b(B[2]), .out(xor_1_out[2]), .cin(adder_1_cout), .cout(adder_2_cout));
  Adder #(.width(1)) adder_3 (.a(not_1_out[3]), .b(B[3]), .out(xor_1_out[3]), .cin(adder_2_cout), .cout(adder_3_cout));
  Adder #(.width(1)) adder_4 (.a(not_1_out[4]), .b(B[4]), .out(xor_1_out[4]), .cin(adder_3_cout), .cout(adder_4_cout));
  Adder #(.width(1)) adder_5 (.a(not_1_out[5]), .b(B[5]), .out(xor_1_out[5]), .cin(adder_4_cout), .cout(adder_5_cout));
  Adder #(.width(1)) adder_6 (.a(not_1_out[6]), .b(B[6]), .out(xor_1_out[6]), .cin(adder_5_cout), .cout(adder_6_cout));
  Adder #(.width(1)) adder_7 (.a(not_1_out[7]), .b(B[7]), .out(xor_1_out[7]), .cin(adder_6_cout), .cout(OVERFLOW));
  assign out_3 = ~xor_1_out;  // NOT_Gate not_2, 8 bits wide
endmodule
