// Logisim project Adder_SUbtractor.circ as structural Verilog: 1 circuit, main circuit main
module main (
  input  SUBTRACT,
  input  [7:0] A,
  input  [7:0] B,
  output [7:0] RESULT,
  output OVERFLOW
);

  wire adder_1_cout, adder_2_cout, adder_3_cout, adder_4_cout, adder_5_cout, adder_6_cout, adder_7_cout,
       xor_1_out, xor_2_out, xor_3_out, xor_4_out, xor_5_out, xor_6_out, xor_7_out, xor_8_out;

  xor xor_1 (xor_1_out, B[0], SUBTRACT);
  xor xor_2 (xor_2_out, B[1], SUBTRACT);
  xor xor_3 (xor_3_out, B[2], SUBTRACT);
  xor xor_4 (xor_4_out, B[3], SUBTRACT);
  xor xor_5 (xor_5_out, B[4], SUBTRACT);
  xor xor_6 (xor_6_out, B[5], SUBTRACT);
  xor xor_7 (xor_7_out, B[6], SUBTRACT);
  xor xor_8 (xor_8_out, B[7], SUBTRACT);
  Adder #(.width(1)) adder_1 (.a(xor_1_out), .b(A[0]), .out(RESULT[0]), .cin(SUBTRACT), .cout(adder_1_cout));
  Adder #(.width(1)) adder_2 (.a(xor_2_out), .b(A[1]), .out(RESULT[1]), .cin(adder_1_cout), .cout(adder_2_cout));
  Adder #(.width(1)) adder_3 (.a(xor_3_out), .b(A[2]), .out(RESULT[2]), .cin(adder_2_cout), .cout(adder_3_cout));
  Adder #(.width(1)) adder_4 (.a(xor_4_out), .b(A[3]), .out(RESULT[3]), .cin(adder_3_cout), .cout(adder_4_cout));
  Adder #(.width(1)) adder_5 (.a(xor_5_out), .b(A[4]), .out(RESULT[4]), .cin(adder_4_cout), .cout(adder_5_cout));
  Adder #(.width(1)) adder_6 (.a(xor_6_out), .b(A[5]), .out(RESULT[5]), .cin(adder_5_cout), .cout(adder_6_cout));
  Adder #(.width(1)) adder_7 (.a(xor_7_out), .b(A[6]), .out(RESULT[6]), .cin(adder_6_cout), .cout(adder_7_cout));
  Adder #(.width(1)) adder_8 (.a(xor_8_out), .b(A[7]), .out(RESULT[7]), .cin(adder_7_cout), .cout(OVERFLOW));

  // Notes on the sheet:
  //   Adder - Subtractor. As an adder it is sum A +B. 
  //   As subtractor it is inverting B and perform A - B
endmodule
