// Logisim project Demultiplexor.circ as structural Verilog: 1 circuit, main circuit main
module main (
  input  IN,
  input  sel,
  output out_3,
  output out_4
);

  wire not_1_out;

  not not_1 (not_1_out, sel);
  and and_1 (out_3, IN, sel);
  and and_2 (out_4, IN, not_1_out);
endmodule
