// Logisim project HalfAdder.circ as structural Verilog: 1 circuit, main circuit main
module main (
  input  X,
  input  Y,
  output SUM,
  output carry
);

  xor xor_1 (SUM, X, Y);
  and and_1 (carry, Y, X);
endmodule
