// Logisim project Invertor_XOR.circ as structural Verilog: 1 circuit, main circuit main
module main (
  input  [7:0] in_1,
  input  INVERT,
  output [7:0] out_3
);

  xor xor_1 (out_3[0], in_1[0], INVERT);
  xor xor_2 (out_3[1], in_1[1], INVERT);
  xor xor_3 (out_3[2], in_1[2], INVERT);
  xor xor_4 (out_3[3], in_1[3], INVERT);
  xor xor_5 (out_3[4], in_1[4], INVERT);
  xor xor_6 (out_3[5], in_1[5], INVERT);
  xor xor_7 (out_3[6], in_1[6], INVERT);
  xor xor_8 (out_3[7], in_1[7], INVERT);

  // Notes on the sheet:
  //   ReadMe:
  //    Invertor made from XOR logic gates, with a selector.
endmodule
