// Logisim project Memory_01.circ as structural Verilog: 1 circuit, main circuit main
module main (
  input  [15:0] IN,
  input  load,
  input  in_3,
  input  [7:0] ADDRESS,
  input  Select,
  input  Read_Write,
  input  [7:0] in_7,
  output [15:0] OUT,
  output [7:0] out_9
);

  wire clock_1_out, not_1_out;
  wire [15:0] multiplexer_1_out;

  // RAM8b_main main_1: pin names not known
  Multiplexer #(.width(16), .enable("false")) multiplexer_1 (.in0(OUT), .in1(IN), .out(multiplexer_1_out), .sel(load));
  not not_1 (not_1_out, Read_Write);
  Clock clock_1 (.out(clock_1_out));
  RAM #(.bus("separate")) ram_1 (
    .addr(ADDRESS), .din(in_7), .data(out_9), .str(Read_Write), .sel(Select), .clk(clock_1_out),
    .ld(not_1_out));  // open: clr
  Register #(.width(16), .trigger("high")) register_1 (.D(multiplexer_1_out), .Q(OUT), .clk(in_3));  // open: en, clr
endmodule
