// Logisim project Memory_02.circ as structural Verilog: 1 circuit, main circuit main
module main (
  input  [15:0] IN,
  input  load,
  input  in_3,
  input  [7:0] ADDRESS,
  input  Select,
  input  Read_Write,
  input  [7:0] IN_2,
  output [15:0] OUT,
  output [7:0] OUT_2
);

  wire not_1_out;
  wire [15:0] multiplexer_1_out;

  Multiplexer #(.width(16), .enable("false")) multiplexer_1 (.in0(OUT), .in1(IN), .out(multiplexer_1_out), .sel(load));
  not not_1 (not_1_out, Read_Write);
  Clock clock_1 ();  // open: out
  RAM #(.bus("separate")) ram_1 (
    .addr(ADDRESS), .din(IN_2), .data(OUT_2), .str(Read_Write), .sel(Select), .clk(Read_Write), .ld(not_1_out));  // open: clr
  Register #(.width(16), .trigger("high")) register_1 (.D(multiplexer_1_out), .Q(OUT), .clk(in_3));  // open: en, clr
endmodule
