// Logisim project Multiplexor_in_use.circ as structural Verilog: 1 circuit, main circuit main
module main (
  input  [3:0] in_1,
  input  [3:0] in_2,
  input  [3:0] in_3,
  input  [3:0] in_4,
  input  [1:0] in_5,
  output [3:0] out_6
);

  Multiplexer #(.select(2), .width(4)) multiplexer_1 (
    .in0(in_1), .in1(in_2), .in2(in_3), .in3(in_4), .out(out_6), .sel(in_5));  // open: en
endmodule
