// Logisim project Multiplexor_minimized.circ as structural Verilog: 1 circuit, main circuit main
module main (
  input  A,
  input  Sel,
  input  B,
  input  A_2,
  input  B_2,
  input  Sel_2,
  output out_7,
  output out_8
);

  wire and_1_out, and_2_out, not_1_out;

  not not_1 (not_1_out, Sel);
  Multiplexer multiplexer_1 (.in0(A_2), .in1(B_2), .out(out_8), .sel(Sel_2));  // open: en
  and and_1 (and_1_out, A, not_1_out);
  and and_2 (and_2_out, Sel, B);
  or or_1 (out_7, and_1_out, and_2_out);
endmodule
