// Logisim project Multiplexor_non_minimized.circ as structural Verilog: 1 circuit, main circuit MUX
module MUX (
  input  a,
  input  b,
  input  sel,
  output out_4
);

  wire and_1_out, and_2_out, and_3_out, and_4_out, and_5_out, and_6_out, and_7_out, not_1_out, not_2_out,
       not_3_out, or_1_out, or_2_out;

  not not_1 (not_1_out, a);
  not not_2 (not_2_out, b);
  not not_3 (not_3_out, sel);
  and and_1 (and_1_out, a, b);
  and and_2 (and_2_out, a, not_2_out);
  and and_3 (and_3_out, not_1_out, b);
  and and_4 (and_4_out, and_1_out, sel);
  and and_5 (and_5_out, and_1_out, not_3_out);
  and and_6 (and_6_out, not_3_out, and_2_out);
  and and_7 (and_7_out, sel, and_3_out);
  or or_1 (or_1_out, and_4_out, and_5_out);
  or or_2 (or_2_out, and_6_out, and_7_out);
  or or_3 (out_4, or_1_out, or_2_out);
endmodule
