// Logisim project ProgramCounter.circ as structural Verilog: 1 circuit, main circuit main
module main (
  input  [15:0] IN,
  input  load,
  input  in_3,
  output [15:0] out_4
);

  wire [15:0] multiplexer_1_out;

  Multiplexer #(.width(16), .enable("false")) multiplexer_1 (
    .in0(out_4), .in1(IN), .out(multiplexer_1_out), .sel(load));
  Register #(.width(16), .trigger("high")) register_1 (.D(multiplexer_1_out), .Q(out_4), .clk(in_3));  // open: en, clr
endmodule
