// Logisim project RAM_4Kb.circ as structural Verilog: 2 circuits, main circuit main
module main (
  input  [7:0] IN,
  input  load,
  input  [2:0] address,
  input  [7:0] IN_2,
  input  [9:0] address_2,
  input  R_W,
  input  [9:0] address_3,
  input  [7:0] IN_3,
  input  R_W_2,
  input  Enable,
  output [7:0] out_11,
  output [7:0] out_12,
  output [7:0] out_13
);

  wire clock_1_out, demultiplexer_1_out0, demultiplexer_1_out1, demultiplexer_1_out2, demultiplexer_1_out3,
       demultiplexer_1_out4, demultiplexer_1_out5, demultiplexer_1_out6, demultiplexer_1_out7, not_1_out;
  wire [7:0] undriven, undriven_2, undriven_3, undriven_4, undriven_5, undriven_6, undriven_7, undriven_8;

  Demultiplexer #(.select(3), .enable("false")) demultiplexer_1 (
    .out0(demultiplexer_1_out0), .out1(demultiplexer_1_out1), .out2(demultiplexer_1_out2),
    .out3(demultiplexer_1_out3), .out4(demultiplexer_1_out4), .out5(demultiplexer_1_out5),
    .out6(demultiplexer_1_out6), .out7(demultiplexer_1_out7), .in(load), .sel(address));
  not not_1 (not_1_out, R_W_2);
  RAM_1KB ram_1kb_1 (.ADDR(address_2), .IN(IN_2), .R_W(R_W), .OUT(out_12));
  Clock clock_1 (.out(clock_1_out));
  Multiplexer #(.select(3), .width(8), .enable("false")) multiplexer_1 (
    .in0(undriven_8), .in1(undriven_6), .in2(undriven_5), .in3(undriven_3), .in4(undriven), .in5(undriven_2),
    .in6(undriven_4), .in7(undriven_7), .out(out_11));  // open: sel
  RAM #(.addrWidth(10), .bus("separate")) ram_1 (
    .addr(address_3), .din(IN_3), .data(out_13), .str(not_1_out), .sel(Enable), .clk(clock_1_out), .ld(R_W_2));  // open: clr
endmodule

module RAM_1KB (
  input  [9:0] ADDR,
  input  [7:0] IN,
  input  R_W,
  output [7:0] OUT
);

  wire not_1_out, or_1_out;

  not not_1 (not_1_out, R_W);
  or or_1 (or_1_out, R_W, not_1_out);
  RAM #(.addrWidth(10), .bus("separate")) ram_1 (
    .addr(ADDR), .din(IN), .data(OUT), .str(not_1_out), .sel(or_1_out), .clk(R_W), .ld(R_W));  // open: clr
endmodule
