// Logisim project Register-1-bit.circ as structural Verilog: 1 circuit, main circuit main
module main (
  input  D,
  input  CLK,
  output Q,
  output NOT_Q
);

  wire nand_1_out, nand_2_out, not_1_out;

  not not_1 (not_1_out, D);
  nand nand_1 (nand_1_out, D, CLK);
  nand nand_2 (nand_2_out, not_1_out, CLK);
  nand nand_3 (Q, nand_1_out, NOT_Q);
  nand nand_4 (NOT_Q, Q, nand_2_out);
endmodule
