// Logisim project Register_in_use.circ as structural Verilog: 1 circuit, main circuit main
module main (
  input  [15:0] IN,
  input  load,
  input  in_3,
  input  [7:0] in_4,
  input  in_5,
  input  in_6,
  output [15:0] out_7,
  output [7:0] out_8
);

  wire [15:0] multiplexer_1_out;

  Multiplexer #(.width(16), .enable("false")) multiplexer_1 (
    .in0(out_7), .in1(IN), .out(multiplexer_1_out), .sel(load));
  Register #(.width(16), .trigger("high")) register_1 (.D(multiplexer_1_out), .Q(out_7), .clk(in_3));  // open: en, clr
  Register register_2 (.D(in_4), .en(in_5), .Q(out_8), .clk(in_6));  // open: clr
endmodule
