// Logisim project geekCPU_1.circ as structural Verilog: 6 circuits, main circuit main
module main (
  input  in_1,
  input  in_2,
  input  in_3,
  input  in_4,
  input  in_5,
  input  [3:0] in_6,
  input  [3:0] in_7,
  input  [3:0] in_8,
  input  [3:0] in_9,
  input  [3:0] in_10,
  input  in_11,
  input  in_12,
  input  in_13,
  input  in_14,
  input  in_15,
  input  in_16,
  input  [3:0] in_17,
  input  in_18,
  input  in_19,
  input  in_20,
  input  in_21,
  input  in_22,
  input  in_23,
  input  [3:0] in_24,
  input  [3:0] in_25,
  input  in_26,
  input  in_27,
  input  in_28,
  output [3:0] out_29,
  output [3:0] out_30,
  output [3:0] out_31
);

  wire button_1_out, button_2_out, clock_1_out, clock_2_out, clock_3_out, clock_4_out, counter_1_out_4,
       counter_1_out_5, counter_2_out_4, counter_2_out_5, counter_3_out_4, counter_3_out_5,
       n4xadder_1_out_14, n4xadder_2_out_14, n4xadder_3_out_14, not_1_out, not_2_out, not_3_out, not_4_out,
       not_5_out, not_6_out, not_8_out, not_9_out, not_10_out, not_11_out, not_12_out, not_13_out,
       not_15_out, not_16_out;
  wire [0:0] n2xmux_3_out_10, n2xmux_8_out_10;
  wire [1:0] counter_1_out_2, counter_2_out_2, counter_3_out_2;
  wire [3:0] n2xmux_1_out_10, n2xmux_4_out_10, n2xmux_6_out_10, n4xadder_1_out_10, n4xadder_2_out_10,
       n4xadder_3_out_10, n4xtrigger_1_out_7, n4xtrigger_2_out_7, n4xtrigger_3_out_7, ram_1_data, ram_2_data,
       ram_3_data;

  Clock clock_1 (.out(clock_1_out));
  Clock clock_2 (.out(clock_2_out));
  // Probe on n4xadder_1_out_10
  LED led_1 (.in(counter_1_out_2[1]));
  Counter counter_1 (
    .in_1(clock_1_out), .out_2(counter_1_out_2[0]), .out_3(counter_1_out_2[1]), .out_4(counter_1_out_4),
    .out_5(counter_1_out_5));
  Counter counter_2 (
    .in_1(clock_2_out), .out_2(counter_2_out_2[0]), .out_3(counter_2_out_2[1]), .out_4(counter_2_out_4),
    .out_5(counter_2_out_5));
  _4xAdder u_4xadder_1 (
    .in_1(in_1), .in_2(n4xtrigger_1_out_7[0]), .in_3(in_2), .in_4(n4xtrigger_1_out_7[1]), .in_5(in_3),
    .in_6(n4xtrigger_1_out_7[2]), .in_7(in_4), .in_8(n4xtrigger_1_out_7[3]), .in_9(in_5),
    .out_10(n4xadder_1_out_10[0]), .out_11(n4xadder_1_out_10[1]), .out_12(n4xadder_1_out_10[2]),
    .out_13(n4xadder_1_out_10[3]), .out_14(n4xadder_1_out_14));
  LED led_2 (.in(n4xadder_1_out_10[2]));
  LED led_3 (.in(n4xadder_1_out_10[1]));
  LED led_4 (.in(n4xadder_1_out_10[3]));
  LED led_5 (.in(counter_1_out_2[0]));
  Clock clock_3 (.out(clock_3_out));
  Clock clock_4 (.out(clock_4_out));
  Button button_1 (.out(button_1_out));
  LED led_6 (.in(n4xadder_1_out_10[0]));
  not not_1 (not_1_out, in_11);
  Counter counter_3 (
    .in_1(clock_3_out), .out_2(counter_3_out_2[0]), .out_3(counter_3_out_2[1]), .out_4(counter_3_out_4),
    .out_5(counter_3_out_5));
  not not_2 (not_2_out, out_31[0]);
  not not_3 (not_3_out, out_31[1]);
  not not_4 (not_4_out, out_31[2]);
  not not_5 (not_5_out, out_31[3]);
  _4xTrigger u_4xtrigger_1 (
    .in_1(n4xadder_1_out_10[0]), .in_2(n4xadder_1_out_10[1]), .in_3(n4xadder_1_out_10[2]),
    .in_4(n4xadder_1_out_10[3]), .C(clock_4_out), .R(button_1_out), .out_7(n4xtrigger_1_out_7[0]),
    .out_8(n4xtrigger_1_out_7[1]), .out_9(n4xtrigger_1_out_7[2]), .out_10(n4xtrigger_1_out_7[3]));
  // Probe on n4xtrigger_1_out_7
  LED led_7 (.in(n2xmux_1_out_10[2]));
  LED led_8 (.in(n2xmux_1_out_10[3]));
  _2xMux u_2xmux_1 (
    .in_1(in_6[0]), .in_2(in_7[0]), .in_3(in_8[0]), .in_4(in_9[0]), .in_5(in_6[1]), .in_6(in_7[1]),
    .in_7(in_8[1]), .in_8(in_9[1]), .in_9(counter_1_out_2), .out_10(n2xmux_1_out_10[0]),
    .out_11(n2xmux_1_out_10[1]));
  _2xMux u_2xmux_2 (
    .in_1(in_6[2]), .in_2(in_7[2]), .in_3(in_8[2]), .in_4(in_9[2]), .in_5(in_6[3]), .in_6(in_7[3]),
    .in_7(in_8[3]), .in_8(in_9[3]), .in_9(counter_1_out_2), .out_10(n2xmux_1_out_10[2]),
    .out_11(n2xmux_1_out_10[3]));
  RAM #(.addrWidth(4), .dataWidth(4), .bus("separate")) ram_1 (
    .addr({2'b00, counter_2_out_2}), .din(in_10), .data(ram_1_data), .sel(not_1_out), .clk(not_6_out),
    .ld(in_12));  // open: str, clr
  not not_6 (not_6_out, in_12);
  _2xMux u_2xmux_3 (
    .in_1(in_13), .in_2(in_14), .in_3(in_15), .in_4(in_16), .in_9(counter_2_out_2),
    .out_10(n2xmux_3_out_10[0]));  // open: in_5, in_6, in_7, in_8, out_11
  LED led_9 (.in(n2xmux_4_out_10[1]));
  LED led_10 (.in(n2xmux_4_out_10[3]));
  LED led_11 (.in(n2xmux_4_out_10[2]));
  _2xMux u_2xmux_4 (
    .in_1(out_31[0]), .in_2(not_2_out), .in_5(out_31[1]), .in_6(not_3_out),
    .in_9({1'b0, n2xmux_8_out_10[0]}), .out_10(n2xmux_4_out_10[0]), .out_11(n2xmux_4_out_10[1]));  // open: in_3, in_4, in_7, in_8
  _2xMux u_2xmux_5 (
    .in_1(out_31[2]), .in_2(not_4_out), .in_5(out_31[3]), .in_6(not_5_out),
    .in_9({1'b0, n2xmux_8_out_10[0]}), .out_10(n2xmux_4_out_10[2]), .out_11(n2xmux_4_out_10[3]));  // open: in_3, in_4, in_7, in_8
  LED led_12 (.in(n4xtrigger_1_out_7[1]));
  LED led_13 (.in(n4xtrigger_1_out_7[2]));
  LED led_14 (.in(n4xtrigger_1_out_7[3]));
  // Probe on n2xmux_1_out_10
  LED led_15 (.in(n2xmux_1_out_10[0]));
  LED led_16 (.in(n2xmux_1_out_10[1]));
  assign out_29 = ~ram_1_data;  // NOT_Gate not_7, 4 bits wide
  not not_8 (not_8_out, in_19);
  not not_9 (not_9_out, in_18);
  LED led_17 (.in(n2xmux_4_out_10[0]));
  // Probe on n2xmux_4_out_10
  LED led_18 (.in(n4xtrigger_1_out_7[0]));
  _4xAdder u_4xadder_2 (
    .in_2(n4xtrigger_2_out_7[0]), .in_3(n2xmux_1_out_10[0]), .in_4(n4xtrigger_2_out_7[1]),
    .in_5(n2xmux_1_out_10[1]), .in_6(n4xtrigger_2_out_7[2]), .in_7(n2xmux_1_out_10[2]),
    .in_8(n4xtrigger_2_out_7[3]), .in_9(n2xmux_1_out_10[3]), .out_10(n4xadder_2_out_10[0]),
    .out_11(n4xadder_2_out_10[1]), .out_12(n4xadder_2_out_10[2]), .out_13(n4xadder_2_out_10[3]),
    .out_14(n4xadder_2_out_14));  // open: in_1
  not not_10 (not_10_out, out_29[0]);
  not not_11 (not_11_out, out_29[1]);
  not not_12 (not_12_out, out_29[2]);
  not not_13 (not_13_out, out_29[3]);
  RAM #(.addrWidth(4), .dataWidth(4), .bus("separate")) ram_2 (
    .addr({2'b00, counter_3_out_2}), .din(in_17), .data(ram_2_data), .sel(not_9_out), .clk(not_8_out),
    .ld(in_19));  // open: str, clr
  LED led_19 (.in(n4xadder_3_out_14));
  _4xAdder u_4xadder_3 (
    .in_2(n4xtrigger_3_out_7[0]), .in_3(n2xmux_4_out_10[0]), .in_4(n4xtrigger_3_out_7[1]),
    .in_5(n2xmux_4_out_10[1]), .in_6(n4xtrigger_3_out_7[2]), .in_7(n2xmux_4_out_10[2]),
    .in_8(n4xtrigger_3_out_7[3]), .in_9(n2xmux_4_out_10[3]), .out_10(n4xadder_3_out_10[0]),
    .out_11(n4xadder_3_out_10[1]), .out_12(n4xadder_3_out_10[2]), .out_13(n4xadder_3_out_10[3]),
    .out_14(n4xadder_3_out_14));  // open: in_1
  LED led_20 (.in(n4xadder_2_out_14));
  LED led_21 (.in(n4xadder_2_out_10[3]));
  LED led_22 (.in(n4xadder_2_out_10[2]));
  _4xTrigger u_4xtrigger_2 (
    .in_1(n4xadder_2_out_10[0]), .in_2(n4xadder_2_out_10[1]), .in_3(n4xadder_2_out_10[2]),
    .in_4(n4xadder_2_out_10[3]), .C(clock_1_out), .R(button_2_out), .out_7(n4xtrigger_2_out_7[0]),
    .out_8(n4xtrigger_2_out_7[1]), .out_9(n4xtrigger_2_out_7[2]), .out_10(n4xtrigger_2_out_7[3]));
  Button button_2 (.out(button_2_out));
  LED led_23 (.in(n2xmux_6_out_10[3]));
  _2xMux u_2xmux_6 (
    .in_1(out_29[0]), .in_2(not_10_out), .in_5(out_29[1]), .in_6(not_11_out),
    .in_9({1'b0, n2xmux_3_out_10[0]}), .out_10(n2xmux_6_out_10[0]), .out_11(n2xmux_6_out_10[1]));  // open: in_3, in_4, in_7, in_8
  _2xMux u_2xmux_7 (
    .in_1(out_29[2]), .in_2(not_12_out), .in_5(out_29[3]), .in_6(not_13_out),
    .in_9({1'b0, n2xmux_3_out_10[0]}), .out_10(n2xmux_6_out_10[2]), .out_11(n2xmux_6_out_10[3]));  // open: in_3, in_4, in_7, in_8
  assign out_31 = ~ram_2_data;  // NOT_Gate not_14, 4 bits wide
  _2xMux u_2xmux_8 (
    .in_1(in_20), .in_2(in_21), .in_3(in_22), .in_4(in_23), .in_9(counter_3_out_2),
    .out_10(n2xmux_8_out_10[0]));  // open: in_5, in_6, in_7, in_8, out_11
  LED led_24 (.in(n4xadder_3_out_10[2]));
  LED led_25 (.in(n4xadder_3_out_10[1]));
  LED led_26 (.in(n4xadder_3_out_10[3]));
  _4xTrigger u_4xtrigger_3 (
    .in_1(n4xadder_3_out_10[0]), .in_2(n4xadder_3_out_10[1]), .in_3(n4xadder_3_out_10[2]),
    .in_4(n4xadder_3_out_10[3]), .C(clock_3_out), .R(in_28), .out_7(n4xtrigger_3_out_7[0]),
    .out_8(n4xtrigger_3_out_7[1]), .out_9(n4xtrigger_3_out_7[2]), .out_10(n4xtrigger_3_out_7[3]));
  LED led_27 (.in(n4xtrigger_3_out_7[3]));
  LED led_28 (.in(n4xadder_2_out_10[1]));
  LED led_29 (.in(n4xadder_2_out_10[0]));
  LED led_30 (.in(n4xtrigger_2_out_7[3]));
  LED led_31 (.in(n4xtrigger_2_out_7[2]));
  LED led_32 (.in(n4xtrigger_2_out_7[0]));
  LED led_33 (.in(n4xtrigger_2_out_7[1]));
  LED led_34 (.in(n2xmux_6_out_10[1]));
  LED led_35 (.in(n2xmux_6_out_10[0]));
  LED led_36 (.in(n2xmux_6_out_10[2]));
  LED led_37 (.in(n4xadder_3_out_10[0]));
  // Probe on n4xadder_3_out_10
  LED led_38 (.in(n4xtrigger_3_out_7[1]));
  LED led_39 (.in(n4xtrigger_3_out_7[0]));
  LED led_40 (.in(n4xtrigger_3_out_7[2]));
  // Probe on n4xadder_2_out_10
  // Probe on n4xtrigger_2_out_7
  // Probe on n2xmux_6_out_10
  // Probe on n4xtrigger_3_out_7
  not not_15 (not_15_out, in_26);
  not not_16 (not_16_out, in_27);
  RAM #(.addrWidth(4), .dataWidth(4), .bus("separate")) ram_3 (
    .addr(in_24), .din(in_25), .data(ram_3_data), .sel(not_15_out), .clk(not_16_out), .ld(in_27));  // open: str, clr
  assign out_30 = ~ram_3_data;  // NOT_Gate not_17, 4 bits wide

  // Notes on the sheet:
  //   Сброс
endmodule

// 155им3
module _4xAdder (
  input  in_1,
  input  in_2,
  input  in_3,
  input  in_4,
  input  in_5,
  input  in_6,
  input  in_7,
  input  in_8,
  input  in_9,
  output out_10,
  output out_11,
  output out_12,
  output out_13,
  output out_14
);

  wire adder_1_cout, adder_2_cout, adder_3_cout;

  Adder #(.width(1)) adder_1 (.a(in_2), .b(in_3), .out(out_10), .cin(in_1), .cout(adder_1_cout));
  Adder #(.width(1)) adder_2 (.a(in_4), .b(in_5), .out(out_11), .cin(adder_1_cout), .cout(adder_2_cout));
  Adder #(.width(1)) adder_3 (.a(in_6), .b(in_7), .out(out_12), .cin(adder_2_cout), .cout(adder_3_cout));
  Adder #(.width(1)) adder_4 (.a(in_8), .b(in_9), .out(out_13), .cin(adder_3_cout), .cout(out_14));
endmodule

// 155тм8
module _4xTrigger (
  input  in_1,
  input  in_2,
  input  in_3,
  input  in_4,
  input  C,
  input  R,
  output out_7,
  output out_8,
  output out_9,
  output out_10
);

  D_Flip_Flop d_ff_1 (.clk(C), .D(in_1), .Q(out_7), .reset(R));  // open: Qn, preset, en
  D_Flip_Flop d_ff_2 (.clk(C), .D(in_2), .Q(out_8), .reset(R));  // open: Qn, preset, en
  D_Flip_Flop d_ff_3 (.clk(C), .D(in_3), .Q(out_9), .reset(R));  // open: Qn, preset, en
  D_Flip_Flop d_ff_4 (.clk(C), .D(in_4), .Q(out_10), .reset(R));  // open: Qn, preset, en
endmodule

// 155кп2
module _2xMux (
  input  in_1,
  input  in_2,
  input  in_3,
  input  in_4,
  input  in_5,
  input  in_6,
  input  in_7,
  input  in_8,
  input  [1:0] in_9,
  output out_10,
  output out_11
);

  Multiplexer #(.select(2)) multiplexer_1 (
    .in0(in_1), .in1(in_2), .in2(in_3), .in3(in_4), .out(out_10), .sel(in_9));  // open: en
  Multiplexer #(.select(2)) multiplexer_2 (
    .in0(in_5), .in1(in_6), .in2(in_7), .in3(in_8), .out(out_11), .sel(in_9));  // open: en
endmodule

// ие5
module Counter (
  input  in_1,
  output out_2,
  output out_3,
  output out_4,
  output out_5
);

  wire not_1_out;

  Counter_part #(.width(4), .max('hf)) counter_1 (
    .Q({out_5, out_4, out_3, out_2}), .clk(not_1_out));  // open: load, D, count, carry, clr
  not not_1 (not_1_out, in_1);
endmodule

// 155лн1
module _6xNot (
  input  in_1,
  input  in_2,
  input  in_3,
  input  in_4,
  input  in_5,
  input  in_6,
  output out_7,
  output out_8,
  output out_9,
  output out_10,
  output out_11,
  output out_12
);

  not not_1 (out_7, in_1);
  not not_2 (out_8, in_2);
  not not_3 (out_9, in_3);
  not not_4 (out_10, in_4);
  not not_5 (out_11, in_5);
  not not_6 (out_12, in_6);
endmodule
